// Logisim project axiom.circ as structural Verilog
module registers (
  input  [2:0] WCS,
  input  CLK,
  input  [15:0] DI,
  input  Global_WE,
  input  [2:0] RCS,
  output [15:0] DO
);

  wire decoder_1_out0, decoder_1_out1, decoder_1_out2, decoder_1_out3, decoder_1_out4, decoder_1_out5,
       decoder_1_out6, decoder_1_out7, or_1_out, or_2_out, or_3_out, or_4_out, or_5_out, or_6_out, or_7_out,
       or_8_out;
  wire [7:0] bit_extender_1_out;
  wire [15:0] R0_q, R1_q, R2_q, R3_q, R4_q, R5_q, R6_q, R7_q;

  assign bit_extender_1_out = {{7{Global_WE}}, Global_WE};  // Bit_Extender bit_extender_1
  Decoder #(.enable("false"), .select(3)) decoder_1 (
    .out0(decoder_1_out0), .out1(decoder_1_out1), .out2(decoder_1_out2), .out3(decoder_1_out3),
    .out4(decoder_1_out4), .out5(decoder_1_out5), .out6(decoder_1_out6), .out7(decoder_1_out7), .sel(WCS));
  or or_1 (or_1_out, decoder_1_out0, bit_extender_1_out[0]);
  or or_2 (or_2_out, decoder_1_out1, bit_extender_1_out[1]);
  or or_3 (or_3_out, decoder_1_out2, bit_extender_1_out[2]);
  or or_4 (or_4_out, decoder_1_out3, bit_extender_1_out[3]);
  or or_5 (or_5_out, decoder_1_out4, bit_extender_1_out[4]);
  or or_6 (or_6_out, decoder_1_out5, bit_extender_1_out[5]);
  or or_7 (or_7_out, decoder_1_out6, bit_extender_1_out[6]);
  or or_8 (or_8_out, decoder_1_out7, bit_extender_1_out[7]);
  Register #(.width(16)) R0 (.D(DI), .en(or_1_out), .clk(CLK), .Q(R0_q));  // open: clr
  Register #(.width(16)) R4 (.D(DI), .en(or_5_out), .clk(CLK), .Q(R4_q));  // open: clr
  Register #(.width(16)) R1 (.D(DI), .en(or_2_out), .clk(CLK), .Q(R1_q));  // open: clr
  Register #(.width(16)) R5 (.D(DI), .en(or_6_out), .clk(CLK), .Q(R5_q));  // open: clr
  Multiplexer #(.select(3), .width(16)) multiplexer_1 (
    .in0(R0_q), .in1(R1_q), .in2(R2_q), .in3(R3_q), .in4(R4_q), .in5(R5_q), .in6(R6_q), .in7(R7_q), .out(DO),
    .sel(RCS));
  Register #(.width(16)) R2 (.D(DI), .en(or_3_out), .clk(CLK), .Q(R2_q));  // open: clr
  Register #(.width(16)) R6 (.D(DI), .en(or_7_out), .clk(CLK), .Q(R6_q));  // open: clr
  Register #(.width(16)) R3 (.D(DI), .en(or_4_out), .clk(CLK), .Q(R3_q));  // open: clr
  Register #(.width(16)) R7 (.D(DI), .en(or_8_out), .clk(CLK), .Q(R7_q));  // open: clr
endmodule

module main (
);

  registers registers_1 ();  // open: WCS, CLK, DI, Global_WE, RCS, DO
endmodule

module ALU (
  input  [15:0] op1,
  input  [15:0] op2,
  input  [3:0] act,
  output O,
  output DZ,
  output N,
  output Z,
  output [15:0] Y
);

  wire and_2_out, comparator_1_gt, comparator_2_eq, comparator_4_eq, comparator_5_eq, or_2_out;
  wire [15:0] adder_1_out, and_1_out, bit_extender_1_out, divider_1_out, divider_1_rem, multiplier_1_cout,
       multiplier_1_out, negator_1_out, not_1_out, or_1_out, shifter_1_out, shifter_2_out, subtractor_1_out,
       undriven, xor_1_out;

  Adder #(.width(16)) adder_1 (
    .a(op1), .b({op2[15:4], op2[7:4]}), .out(adder_1_out), .cout(multiplier_1_cout[15]));  // open: cin
  Subtractor #(.width(16)) subtractor_1 (
    .a(op1), .b({op2[15:4], op2[7:4]}), .out(subtractor_1_out), .bout(N));  // open: bin
  Multiplier #(.width(16)) multiplier_1 (
    .a(op1), .b({op2[15:4], op2[7:4]}), .out(multiplier_1_out), .cout(multiplier_1_cout));  // open: cin
  Divider #(.width(16)) divider_1 (
    .a(op1), .b({op2[15:4], op2[7:4]}), .out(divider_1_out), .rem(divider_1_rem));  // open: upper
  Negator #(.width(16)) negator_1 (.in(op1), .out(negator_1_out));
  Comparator #(.width(16)) comparator_1 (
    .a(op1), .b({op2[15:4], op2[7:4]}), .gt(comparator_1_gt), .eq(comparator_1_gt), .lt(comparator_1_gt));
  assign not_1_out = ~op1;  // NOT_Gate not_1, 16 bits wide
  assign and_1_out = op1 & {op2[15:4], op2[7:4]};  // AND_Gate and_1, 16 bits wide
  assign or_1_out = op1 | {op2[15:4], op2[7:4]};  // OR_Gate or_1, 16 bits wide
  assign xor_1_out = op1 ^ {op2[15:4], op2[7:4]};  // XOR_Gate xor_1, 16 bits wide
  Shifter #(.width(16)) shifter_1 (.in(op1), .\dist (op2[7:4]), .out(shifter_1_out));
  Shifter #(.shift("lr"), .width(16)) shifter_2 (.in(op1), .\dist (op2[7:4]), .out(shifter_2_out));
  assign bit_extender_1_out = {{15{comparator_1_gt}}, comparator_1_gt};  // Bit_Extender bit_extender_1
  Comparator #(.width(16)) comparator_2 (
    .a({16{1'b0}}), .b({op2[15:4], op2[7:4]}), .eq(comparator_2_eq));  // open: gt, lt
  Multiplexer #(.select(4), .width(16)) multiplexer_1 (
    .in1(adder_1_out), .in2(subtractor_1_out), .in3(multiplier_1_out), .in4(divider_1_out),
    .in5(divider_1_rem), .in6(negator_1_out), .in7(bit_extender_1_out), .in8(not_1_out), .in9(and_1_out),
    .in10(or_1_out), .in11(xor_1_out), .in12(undriven), .in13(shifter_2_out), .out(Y), .sel(act));  // open: in0, in14, in15
  Comparator #(.width(16)) comparator_3 (.a({16{1'b0}}), .b(Y), .eq(Z));  // open: gt, lt
  Comparator #(.width(4)) comparator_4 (.a(act), .b(4'b0100), .eq(comparator_4_eq));  // open: gt, lt
  Comparator #(.width(4)) comparator_5 (.a(act), .b(4'b0101), .eq(comparator_5_eq));  // open: gt, lt
  buf and_2 (and_2_out, comparator_2_eq);  // AND_Gate
  or or_2 (or_2_out, comparator_4_eq, comparator_5_eq);
  and and_3 (DZ, and_2_out, or_2_out);

  assign op2[3:0] = op2[7:4];
endmodule

module Core (
);

  ALU alu_1 (.op1({16{1'b1}}), .op2({16{1'b1}}), .act(4'b0001));  // open: O, DZ, N, Z, Y
  // Probe on nothing
  Register register_1 ();  // open: D, en, clk, Q, clr
endmodule
